// Logisim project Contador.circ as structural Verilog: 1 circuit, main circuit main
module main (
  input  Clear,
  input  Enable,
  input  Reloj,
  output [7:0] out_4
);

  wire comparator_2_eq, or_1_out;

  or or_1 (or_1_out, Clear, comparator_2_eq);
  Counter counter_1 (
    .load(or_1_out), .up(1'b1), .count(Enable), .clk(Reloj), .D(8'h30), .Q(out_4));  // open: clr, carry
  Comparator comparator_1 (.a(8'h34), .b(out_4));  // open: gt, eq, lt
  Comparator comparator_2 (.a(out_4), .b(8'h37), .eq(comparator_2_eq));  // open: gt, lt

  // Notes on the sheet:
  //   El "Clear" reseteara a 48, NO 0
  //   Si fuera 55, reseteamos en el proximo tick
  //   if 52 == salida del contador then sumar 52 + 3 (a completar :))
endmodule
