// Logisim project Proyecto.circ as structural Verilog: 4 circuits, main circuit main
module main (
);

  wire full_adder_1_g, full_adder_1_p, full_adder_2_g, full_adder_2_p, full_adder_3_g, full_adder_3_p,
       full_adder_4_g, full_adder_4_p, full_adder_5_g, full_adder_5_p, full_adder_6_g, full_adder_6_p,
       full_adder_7_g, full_adder_7_p, full_adder_8_g, full_adder_8_p, undriven, undriven_2, undriven_3,
       undriven_4, undriven_5, undriven_6, undriven_7, undriven_8, undriven_9, undriven_10, undriven_11,
       undriven_12, undriven_13, undriven_14, undriven_15, undriven_16, undriven_17, undriven_18,
       undriven_19, undriven_20, undriven_21, undriven_22, undriven_23, undriven_24;

  Full_Adder full_adder_1 (
    .A(undriven_3), .B(undriven), .Carry_in(undriven_2), .P(full_adder_1_p), .G(full_adder_1_g));  // open: S
  Full_Adder full_adder_2 (
    .A(undriven_6), .B(undriven_4), .Carry_in(undriven_5), .P(full_adder_2_p), .G(full_adder_2_g));  // open: S
  Full_Adder full_adder_3 (
    .A(undriven_9), .B(undriven_7), .Carry_in(undriven_8), .P(full_adder_3_p), .G(full_adder_3_g));  // open: S
  Full_Adder full_adder_4 (
    .A(undriven_12), .B(undriven_10), .Carry_in(undriven_11), .P(full_adder_4_p), .G(full_adder_4_g));  // open: S
  Full_Adder full_adder_5 (
    .A(undriven_15), .B(undriven_13), .Carry_in(undriven_14), .P(full_adder_5_p), .G(full_adder_5_g));  // open: S
  Full_Adder full_adder_6 (
    .A(undriven_18), .B(undriven_16), .Carry_in(undriven_17), .P(full_adder_6_p), .G(full_adder_6_g));  // open: S
  Full_Adder full_adder_7 (
    .A(undriven_21), .B(undriven_19), .Carry_in(undriven_20), .P(full_adder_7_p), .G(full_adder_7_g));  // open: S
  Bloque_B bloque_b_1 ();  // open: PL, GL, Cin, PH, GH, CH, CL, GHL, PHL
  Full_Adder full_adder_8 (
    .A(undriven_24), .B(undriven_22), .Carry_in(undriven_23), .P(full_adder_8_p), .G(full_adder_8_g));  // open: S
  Bloque_B bloque_b_2 (
    .PL(full_adder_8_p), .GL(full_adder_8_g), .Cin(1'b1), .PH(full_adder_7_p), .GH(full_adder_7_g));  // open: CH, CL, GHL, PHL

  // Notes on the sheet:
  //   A7B7
  //   A5B5
  //   A4B4
  //   A3B3
  //   A2B2
  //   A1B1
  //   A0B0
endmodule

module LATA (
  input  C0
);

  wire A_p1, A_p2, A_p3, A_p4, A_p5, A_p6, A_p7, A_p8, and_1_out, and_2_out, and_3_out, and_4_out, and_5_out,
       and_6_out, and_7_out, B_p1, B_p2, B_p3, B_p4, B_p5, B_p6, B_p7, B_p8, CH1_out, CH3_2_out, CH3_out,
       CH5_out, CH7_6_out, CH7_out, CH_out, G0_out, G1_0_out, G1_out, G2_out, G3_0_out, G3_2_out, G3_out,
       G4_out, G5_4_out, G5_out, G6_out, G7_4_out, G7_6_out, G7_out, or_1_out, or_2_out, or_3_out, or_4_out,
       or_5_out, or_6_out, or_7_out, P0_out, P1_0_out, P1_out, P2_out, P3_0_out, P3_2_out, P3_out, P4_out,
       P5_4_out, P5_out, P6_out, P7_4_out, P7_6_out, P7_out, xor_1_out, xor_2_out, xor_3_out, xor_4_out,
       xor_5_out, xor_6_out, xor_7_out, xor_8_out;

  // DipSwitch A: pin names not known; wires that end beside it: A_p1, A_p2, A_p3, A_p4, A_p5, A_p6, A_p7, A_p8
  and G7 (G7_out, A_p8, B_p8);
  xor xor_1 (xor_1_out, A_p8, B_p8);
  or P7 (P7_out, A_p8, B_p8);
  // DipSwitch B: pin names not known; wires that end beside it: B_p1, B_p2, B_p3, B_p4, B_p5, B_p6, B_p7, B_p8
  // XOR_Gate S7 has open pins: in0=xor_1_out, in1=CH7_out, out=open
  and P7_6 (P7_6_out, P6_out, P7_out);
  or or_1 (or_1_out, P6_out, G6_out);
  and and_1 (and_1_out, G6_out, P7_out);
  and CH7 (CH7_out, or_1_out, CH7_6_out);
  or G7_6 (G7_6_out, and_1_out, G7_out);
  and G6 (G6_out, A_p7, B_p7);
  xor xor_2 (xor_2_out, A_p7, B_p7);
  or P6 (P6_out, A_p7, B_p7);
  // XOR_Gate S6 has open pins: in0=xor_2_out, in1=CH7_6_out, out=open
  and P7_4 (P7_4_out, P5_4_out, P7_6_out);
  and and_2 (and_2_out, G5_4_out, P7_6_out);
  or or_2 (or_2_out, P4_out, G4_out);
  or G7_4 (G7_4_out, and_2_out, G7_6_out);
  xor xor_3 (xor_3_out, A_p6, B_p6);
  and CH5 (CH5_out, or_2_out, CH_out);
  or or_3 (or_3_out, P5_4_out, G5_4_out);
  // XOR_Gate S5 has open pins: in0=xor_3_out, in1=CH5_out, out=open
  or P5 (P5_out, A_p6, B_p6);
  and G5 (G5_out, A_p6, B_p6);
  and CH7_6 (CH7_6_out, or_3_out, CH_out);
  and P5_4 (P5_4_out, P4_out, P5_out);
  and and_3 (and_3_out, G4_out, P5_out);
  xor xor_4 (xor_4_out, A_p5, B_p5);
  or G5_4 (G5_4_out, and_3_out, G5_out);
  // XOR_Gate S4 has open pins: in0=xor_4_out, in1=CH_out, out=open
  or P4 (P4_out, A_p5, B_p5);
  and G4 (G4_out, A_p5, B_p5);
  xor xor_5 (xor_5_out, A_p4, B_p4);
  // XOR_Gate S3 has open pins: in0=xor_5_out, in1=CH3_out, out=open
  or P3 (P3_out, A_p4, B_p4);
  and G3 (G3_out, A_p4, B_p4);
  or or_4 (or_4_out, P2_out, G2_out);
  // AND_Gate P7_0 has open pins: in0=P3_0_out, in1=P7_4_out, out=open
  and and_4 (and_4_out, G3_0_out, P7_4_out);
  and CH3 (CH3_out, or_4_out, CH3_2_out);
  // OR_Gate G7_0 has open pins: in0=and_4_out, in1=G7_4_out, out=open
  or or_5 (or_5_out, P3_0_out, G3_0_out);
  and P3_2 (P3_2_out, P2_out, P3_out);
  and and_5 (and_5_out, G2_out, P3_out);
  and CH (CH_out, or_5_out, C0);
  or G3_2 (G3_2_out, and_5_out, G3_out);
  xor xor_6 (xor_6_out, A_p3, B_p3);
  // XOR_Gate S2 has open pins: in0=xor_6_out, in1=CH3_2_out, out=open
  or or_6 (or_6_out, P1_0_out, G1_0_out);
  or P2 (P2_out, A_p3, B_p3);
  and G2 (G2_out, A_p3, B_p3);
  and CH3_2 (CH3_2_out, or_6_out, C0);
  and P3_0 (P3_0_out, P1_0_out, P3_2_out);
  and and_6 (and_6_out, G1_0_out, P3_2_out);
  or or_7 (or_7_out, P0_out, G0_out);
  xor xor_7 (xor_7_out, A_p2, B_p2);
  and CH1 (CH1_out, or_7_out, C0);
  or G3_0 (G3_0_out, and_6_out, G3_2_out);
  // XOR_Gate S1 has open pins: in0=xor_7_out, in1=CH1_out, out=open
  or P1 (P1_out, A_p2, B_p2);
  and G1 (G1_out, A_p2, B_p2);
  and P1_0 (P1_0_out, P0_out, P1_out);
  and and_7 (and_7_out, G0_out, P1_out);
  xor xor_8 (xor_8_out, A_p1, B_p1);
  or G1_0 (G1_0_out, and_7_out, G1_out);
  // XOR_Gate S0 has open pins: in0=xor_8_out, in1=C0, out=open
  or P0 (P0_out, A_p1, B_p1);
  and G0 (G0_out, A_p1, B_p1);

  // Notes on the sheet:
  //   Cin
  //   FA7
  //   PL
  //   PH
  //   GL
  //   GH
  //   Cin
  //   CL
  //   Cin
  //   FA6
  //   PH
  //   Cin
  //   GL
  //   GH
  //   FA5
  //   PL
  //   Cin
  //   CL
  //   Cin
  //   Cin
  //   PL
  //   PH
  //   GH
  //   GL
  //   FA4
  //   Los C de cada FA son los Cin que están diagramados en el PDF del proyecto, es decir, dependen de los niveles más altos, hay que unirlos cuando estén hechos
  //   Cin
  //   CL
  //   FA3
  //   PH
  //   GH
  //   PL
  //   GL
  //   Cin
  //   PL
  //   PH
  //   CL
  //   GL
  //   GH
  //   FA2
  //   CL
  //   Cin
  //   Cin
  //   PH
  //   PL
  //   GL
  //   GH
  //   Cin
  //   CL
  //   FA1
  //   Cin
  //   Cin
  //   PL
  //   PH
  //   GL
  //   GH
  //   CL
  //   FA0
endmodule

module Full_Adder (
  input  A,
  input  B,
  input  Carry_in,
  output P,
  output S,
  output G
);

  wire and_2_out, or_1_out;

  xor xor_1 (P, A, B);
  and and_1 (G, B, A);
  and and_2 (and_2_out, P, Carry_in);
  xor xor_2 (S, P, Carry_in);
  or or_1 (or_1_out, and_2_out, G);

  // Notes on the sheet:
  //   P0
  //   P0*Cin
  //   Carry_Out (Sin uso)
endmodule

module Bloque_B (
  input  PH,
  input  GH,
  input  PL,
  input  GL,
  input  Cin,
  output GHL,
  output PHL,
  output CH,
  output CL
);

  wire and_1_out, and_3_out;

  and and_1 (and_1_out, PH, GL);
  and and_2 (PHL, PH, PL);
  and and_3 (and_3_out, PL, Cin);
  or or_1 (GHL, GH, and_1_out);
  or or_2 (CH, GL, and_3_out);

  assign CL = 1'b1;
endmodule
